// Logisim project subleq.circ as structural Verilog: 4 circuits, main circuit read_operand
module main (
);

  wire _0_out, _1_out, _2_out, _3_out, _4_out, _5_out, _6_out, _7_out, _8_out, _9_out, A_out, and_1_out,
       B_out, button_2_out, button_3_out, button_4_out, button_out, C_out, clock_1_out, cpu_1_halt,
       cpu_1_mem_write, D_out, E_out, F_out, multiplexer_2_out, not_1_out, or_1_out, or_2_out, or_3_out,
       priority_encoder_1_gs, RST_out;
  wire [3:0] priority_encoder_1_out, shift_register_1_q2, shift_register_1_q4;
  wire [7:0] addr_sel_1_addr, controlled_buffer_1_out, cpu_1_mem_addr;
  wire [23:0] cpu_1_mem_out, multiplexer_1_out, ram_1_data, shift_register_1_q0;

  LED HALT (.in(cpu_1_halt));
  Button RST (.out(RST_out));
  Hex_Digit_Display hex_digit_display_1 (.value(shift_register_1_q0[23:20]));  // open: dp
  Button button (.out(button_out));
  Button button_2 (.out(button_2_out));
  Hex_Digit_Display hex_digit_display_2 (.value(shift_register_1_q4));  // open: dp
  Button _1 (.out(_1_out));
  Button _2 (.out(_2_out));
  Button _5 (.out(_5_out));
  Button _4 (.out(_4_out));
  Button _8 (.out(_8_out));
  Button _7 (.out(_7_out));
  Button _0 (.out(_0_out));
  Button button_3 (.out(button_3_out));
  Button A (.out(A_out));
  Button B (.out(B_out));
  Button E (.out(E_out));
  Button D (.out(D_out));
  or or_1 (or_1_out, button_4_out, button_3_out, button_out, button_2_out);
  and and_1 (and_1_out, button_4_out, cpu_1_halt);
  Hex_Digit_Display hex_digit_display_3 (.value(shift_register_1_q0[15:12]));  // open: dp
  Hex_Digit_Display hex_digit_display_4 (.value(shift_register_1_q2));  // open: dp
  Button _3 (.out(_3_out));
  Button _6 (.out(_6_out));
  Button _9 (.out(_9_out));
  Button button_4 (.out(button_4_out));
  Button C (.out(C_out));
  Button F (.out(F_out));
  addr_sel addr_sel_1 (
    .in_2(button_out), .in_3(button_2_out), .ADDR(addr_sel_1_addr), .ADDR_IN(controlled_buffer_1_out),
    .Pause(cpu_1_halt), .CLK(multiplexer_2_out));
  Clock clock_1 (.out(clock_1_out));
  assign controlled_buffer_1_out = cpu_1_halt ? addr_sel_1_addr : 8'bz;  // Controlled_Buffer controlled_buffer_1
  Multiplexer #(.width(24), .enable("false")) multiplexer_1 (
    .in0(cpu_1_mem_out),
    .in1({shift_register_1_q0[23:20], shift_register_1_q4, shift_register_1_q0[15:12], shift_register_1_q2, shift_register_1_q0[7:0]}),
    .out(multiplexer_1_out), .sel(cpu_1_halt));
  assign controlled_buffer_1_out = not_1_out ? cpu_1_mem_addr : 8'bz;  // Controlled_Buffer controlled_buffer_2
  not not_1 (not_1_out, cpu_1_halt);
  Hex_Digit_Display hex_digit_display_5 (.value(shift_register_1_q0[7:4]));  // open: dp
  Multiplexer #(.enable("false")) multiplexer_2 (
    .in0(clock_1_out), .in1(or_1_out), .out(multiplexer_2_out), .sel(cpu_1_halt));
  or or_2 (or_2_out, and_1_out, cpu_1_mem_write);
  CPU cpu_1 (
    .HALT(cpu_1_halt), .RST(RST_out), .CLK(multiplexer_2_out), .MEM_ADDR(cpu_1_mem_addr),
    .MEM_IN(ram_1_data), .MEM_OUT(cpu_1_mem_out), .MEM_WRITE(cpu_1_mem_write));  // open: ENABLE
  Hex_Digit_Display hex_digit_display_6 (.value(shift_register_1_q0[3:0]));  // open: dp
  Priority_Encoder #(.select(4), .disabled(0)) priority_encoder_1 (
    .in0(_0_out), .in1(_1_out), .in2(_2_out), .in3(_3_out), .in4(_4_out), .in5(_5_out), .in6(_6_out),
    .in7(_7_out), .in8(_8_out), .in9(_9_out), .in10(A_out), .in11(B_out), .in12(C_out), .in13(D_out),
    .in14(E_out), .in15(F_out), .out(priority_encoder_1_out), .gs(priority_encoder_1_gs));  // open: en_out, en_in
  RAM #(.dataWidth(24), .bus("separate")) ram_1 (
    .addr(controlled_buffer_1_out), .din(multiplexer_1_out), .data(ram_1_data), .str(or_2_out),
    .clk(multiplexer_2_out));  // open: sel, ld, clr
  Shift_Register #(.width(4), .length(6)) shift_register_1 (
    .shift(priority_encoder_1_gs), .in(priority_encoder_1_out), .clk(or_3_out), .load(multiplexer_2_out),
    .d0(ram_1_data[3:0]), .q0(shift_register_1_q0[3:0]), .d1(ram_1_data[7:4]), .q1(shift_register_1_q0[7:4]),
    .d2(ram_1_data[11:8]), .q2(shift_register_1_q2), .d3(ram_1_data[15:12]), .q3(shift_register_1_q0[15:12]),
    .d4(ram_1_data[19:16]), .q4(shift_register_1_q4), .d5(ram_1_data[23:20]), .q5(shift_register_1_q0[23:20]));  // open: out, clr
  or or_3 (or_3_out, priority_encoder_1_gs, multiplexer_2_out);
  Hex_Digit_Display hex_digit_display_7 (.value(addr_sel_1_addr[7:4]));  // open: dp
  Hex_Digit_Display hex_digit_display_8 (.value(addr_sel_1_addr[3:0]));  // open: dp
endmodule

module read_operand (
  input  [23:0] MEM_IN,
  input  [7:0] MEMADDR_IN,
  input  Enable,
  input  CLK,
  input  CLR,
  output [7:0] MEM_ADDR,
  output [23:0] OUT
);

  assign MEM_ADDR = Enable ? MEMADDR_IN : 8'bz;  // Controlled_Buffer controlled_buffer_1
  Register #(.width(24)) PC (.D(MEM_IN), .en(Enable), .Q(OUT), .clk(CLK), .clr(CLR));

  // Notes on the sheet:
  //   MEM_ADDR: pull=down
endmodule

module CPU (
  input  [23:0] MEM_IN,
  input  ENABLE,
  input  CLK,
  input  RST,
  output [7:0] MEM_ADDR,
  output MEM_WRITE,
  output [23:0] MEM_OUT,
  output HALT
);

  wire and_1_out, comparator_2_eq, comparator_2_lt, demultiplexer_1_out0, demultiplexer_1_out1,
       demultiplexer_1_out2, not_1_out, not_2_out, not_3_out, or_1_out;
  wire [1:0] STEP_q;
  wire [7:0] adder_1_out, controlled_buffer_1_out, INS_2_out, INS_2_out_2, INS_2_out_3, PC_q;
  wire [23:0] A_2_out, B_2_out, subtractor_1_out;

  // Probe on PC_q
  // Probe on controlled_buffer_1_out
  Demultiplexer #(.select(2), .disabled(0), .enable("false")) demultiplexer_1 (
    .out0(demultiplexer_1_out0), .out1(demultiplexer_1_out1), .out2(demultiplexer_1_out2), .out3(MEM_WRITE),
    .in(not_1_out), .sel(STEP_q));
  not not_1 (not_1_out, and_1_out);
  Comparator #(.mode("unsigned")) comparator_1 (.a({8{1'b1}}), .b(PC_q), .eq(HALT));  // open: gt, lt
  Adder adder_1 (.a(PC_q), .b(controlled_buffer_1_out), .out(adder_1_out));  // open: cin, cout
  assign controlled_buffer_1_out = or_1_out ? INS_2_out : 8'bz;  // Controlled_Buffer controlled_buffer_1
  assign controlled_buffer_1_out = not_2_out ? 8'h1 : 8'bz;  // Controlled_Buffer controlled_buffer_2
  not not_2 (not_2_out, or_1_out);
  Counter #(.width(2), .max('h3), .trigger("falling")) STEP (
    .Q(STEP_q), .clk(and_1_out));  // open: load, D, count, carry, clr
  not not_3 (not_3_out, HALT);
  Register PC (.D(adder_1_out), .en(MEM_WRITE), .Q(PC_q), .clk(and_1_out), .clr(RST));
  assign MEM_ADDR = MEM_WRITE ? INS_2_out_2 : 8'bz;  // Controlled_Buffer controlled_buffer_3
  // Probe on {INS_2_out_3, INS_2_out_2, INS_2_out}
  // Probe on B_2_out
  read_operand INS_2 (
    .MEMADDR_IN(PC_q), .OUT({INS_2_out_3, INS_2_out_2, INS_2_out}), .MEM_ADDR(MEM_ADDR), .MEM_IN(MEM_IN),
    .Enable(demultiplexer_1_out0), .CLK(and_1_out), .CLR(RST));
  // Probe on A_2_out
  read_operand B_2 (
    .MEMADDR_IN(INS_2_out_2), .OUT(B_2_out), .MEM_ADDR(MEM_ADDR), .MEM_IN(MEM_IN),
    .Enable(demultiplexer_1_out1), .CLK(and_1_out), .CLR(RST));
  read_operand A_2 (
    .MEMADDR_IN(INS_2_out_3), .OUT(A_2_out), .MEM_ADDR(MEM_ADDR), .MEM_IN(MEM_IN),
    .Enable(demultiplexer_1_out2), .CLK(and_1_out), .CLR(RST));
  assign MEM_OUT = MEM_WRITE ? subtractor_1_out : 24'bz;  // Controlled_Buffer controlled_buffer_4
  Subtractor #(.width(24)) subtractor_1 (.a(B_2_out), .b(A_2_out), .out(subtractor_1_out));  // open: bin, bout
  // Probe on subtractor_1_out
  Comparator #(.width(24)) comparator_2 (
    .a(subtractor_1_out), .b({24{1'b0}}), .eq(comparator_2_eq), .lt(comparator_2_lt));  // open: gt
  and and_1 (and_1_out, not_3_out, ENABLE, CLK);
  or or_1 (or_1_out, comparator_2_eq, comparator_2_lt);

  // Notes on the sheet:
  //   RST: pull=down
  //   ENABLE: pull=up
endmodule

module addr_sel (
  input  [7:0] ADDR_IN,
  input  in_2,
  input  in_3,
  input  Pause,
  input  CLK,
  output [7:0] ADDR
);

  wire and_1_out, or_1_out, or_2_out;

  or or_1 (or_1_out, in_2, in_3);
  or or_2 (or_2_out, in_2, ~Pause);  // OR_Gate
  and and_1 (and_1_out, or_1_out, Pause);
  Counter counter_1 (.load(or_2_out), .D(ADDR_IN), .count(and_1_out), .Q(ADDR), .clk(CLK));  // open: carry, clr
endmodule
